# Fritzing sketch circuit-design (saved by Fritzing 1.0.1rc)
breadboards: 1

parts:
  Part1 = Arduino Uno (Rev3)
  Q1 = NPN-Transistor [package="TO92 [THT]"]
  Q3 = NPN-Transistor [package="TO92 [THT]"]
  Q4 = NPN-Transistor [package="TO92 [THT]"]
  U1 = Vibration Motor- ROB-08449 [package=vibe-motor-10mm]
  U3 = Vibration Motor- ROB-08449 [package=vibe-motor-10mm]
  U4 = Vibration Motor- ROB-08449 [package=vibe-motor-10mm]
  BT1 = Bluetooth HC-06u
  BAT1 = BC9VPC [package=bc9vpc]  # not connected
  R1 = Resistor [tolerance=±5% resistance=1k package="2010 [SMD]"]
  R2 = Resistor [tolerance=±5% resistance=1k package="0805 [SMD]"]
  R3 = Resistor [tolerance=±5% resistance=2.2k package="2512 [SMD]"]
  R4 = Resistor [tolerance=±5% resistance=33 package="0402 [SMD]"]
  R5 = Resistor [tolerance=±5% resistance=33 package="0402 [SMD]"]
  R6 = Resistor [tolerance=±5% resistance=1k package="0805 [SMD]"]
  R7 = Resistor [tolerance=±5% resistance=33 package="0402 [SMD]"]
  R8 = Resistor [tolerance=±5% resistance=1k package="0805 [SMD]"]

nets:
  N1: Part1.D10_PWM/SS, R6.Pin_1
  N2: Part1.D2, BT1.connector2
  N3: Part1.D3_PWM, R1.Pin_0
  N4: Part1.D5_PWM, R2.Pin_1
  N5: Part1.D6_PWM, R8.Pin_1
  N6: Part1.5V, BT1.connector0, R4.Pin_1, R5.Pin_1, R7.Pin_1
  N7: Part1.GND, Q1.E, Q3.E, Q4.E, BT1.connector1, R3.Pin_1
  N8: Q1.B, R2.Pin_0
  N9: Q1.C, U1.+
  N10: Q3.B, R6.Pin_0
  N11: Q3.C, U3.+
  N12: Q4.B, R8.Pin_0
  N13: Q4.C, U4.+
  N14: U1.-, R4.Pin_0
  N15: U3.-, R7.Pin_0
  N16: U4.-, R5.Pin_0
  N17: BT1.connector3, R1.Pin_1, R3.Pin_0
