# Fritzing sketch updated-circuit-design (saved by Fritzing 1.0.1rc)
breadboards: 1

parts:
  Part1 = Bluetooth HC-05 Macho
  Part2 = Arduino Uno (Rev3) - ICSP
  R1 = Resistor [tolerance=±5% resistance=1k package="0603 [SMD]"]
  R2 = Resistor [tolerance=±5% resistance=2.2k package="0603 [SMD]"]
  Q1 = NPN-Transistor [package="TO92 [THT]"]
  U1 = Vibration Motor- ROB-08449 [package=vibe-motor-10mm]
  VCC1 = Battery block 9V  # not connected
  Q2 = NPN-Transistor [package="TO92 [THT]"]
  Q3 = NPN-Transistor [package="TO92 [THT]"]
  R3 = Resistor [tolerance=±5% resistance=1k package="0603 [SMD]"]
  R4 = Resistor [tolerance=±5% resistance=1k package="0603 [SMD]"]
  R5 = Resistor [tolerance=±5% resistance=1k package="0603 [SMD]"]
  R6 = Resistor [tolerance=±5% resistance=33 package="0603 [SMD]"]
  R7 = Resistor [tolerance=±5% resistance=33 package="0603 [SMD]"]
  R8 = Resistor [tolerance=±5% resistance=33 package="0603 [SMD]"]
  U2 = Vibration Motor- ROB-08449 [package=vibe-motor-10mm]
  U3 = Vibration Motor- ROB-08449 [package=vibe-motor-10mm]

nets:
  N1: Part1.TXD, Part2.D2
  N2: Part1.RXD, R1.Pin_0, R2.Pin_0
  VCC: Part1.VCC, Part2.5V, U1.-, R6.Pin_0, R6.Pin_1, R7.Pin_0, R7.Pin_1, R8.Pin_0, R8.Pin_1, U2.-, U3.-
  GND: Part1.GND, Part2.GND, R2.Pin_1, Q1.C, Q2.C, Q3.C
  N3: Part2.D9_PWM, R4.Pin_1
  N4: Part2.D10_PWM/SS, R3.Pin_1
  N5: Part2.D3_PWM, R1.Pin_1
  N6: Part2.D6_PWM, R5.Pin_1
  N7: Q1.E, U2.+
  N8: Q1.B, R3.Pin_0
  N9: U1.+, Q3.E
  N10: Q2.E, U3.+
  N11: Q2.B, R5.Pin_0
  N12: Q3.B, R4.Pin_0
